// Logisim project Traffic_Light_Implementation.circ as structural Verilog: 2 circuits, main circuit main
module main (
  input  Pedestrian
);

  wire A_q, A_qn, and_1_out, and_2_out, and_3_out, and_4_out, and_5_out, and_6_out, and_7_out, and_8_out,
       and_9_out, B_q, B_qn, clk_out, comparator_1_eq, comparator_2_eq, multiplexer_1_out, or_1_out,
       or_2_out, or_3_out, or_4_out, Reset_out, y_carry;
  wire [3:0] x_q;
  wire [4:0] Y_For_Pedestrain_q;

  Clock clk (.out(clk_out));
  Button Reset (.out(Reset_out));
  Counter #(.max('hf), .width(4)) x (.Q(x_q), .clk(clk_out), .clr(Reset_out));  // open: load, D, count, carry, up
  Counter #(.max('hf), .width(4)) y (.carry(y_carry), .clk(clk_out), .clr(Reset_out));  // open: load, D, count, Q, up
  Counter #(.max('h13), .width(5)) Y_For_Pedestrain (
    .Q(Y_For_Pedestrain_q), .clk(clk_out), .clr(Reset_out));  // open: load, D, count, carry, up
  Comparator #(.mode("unsigned"), .width(4)) comparator_1 (.a(x_q), .b(4'b0101), .eq(comparator_1_eq));  // open: gt, lt
  Comparator #(.mode("unsigned"), .width(5)) comparator_2 (
    .a(Y_For_Pedestrain_q), .b(5'b10011), .eq(comparator_2_eq));  // open: gt, lt
  Multiplexer multiplexer_1 (.in0(y_carry), .in1(comparator_2_eq), .out(multiplexer_1_out), .sel(Pedestrian));
  and and_1 (and_1_out, A_q, ~comparator_1_eq);  // AND_Gate
  and and_2 (and_2_out, A_q, ~B_q, ~multiplexer_1_out);  // AND_Gate
  and and_3 (and_3_out, ~A_q, comparator_1_eq, B_q, ~multiplexer_1_out);  // AND_Gate
  and and_4 (and_4_out, ~comparator_1_eq, multiplexer_1_out);  // AND_Gate
  and and_5 (and_5_out, B_q, ~comparator_1_eq);  // AND_Gate
  or or_1 (or_1_out, and_1_out, and_2_out, and_3_out);
  or or_2 (or_2_out, and_4_out, and_5_out);
  D_Flip_Flop A (.D(or_1_out), .clk(clk_out), .Q(A_q), .Qn(A_qn), .reset(Reset_out));  // open: preset
  D_Flip_Flop B (.D(or_2_out), .clk(clk_out), .Q(B_q), .Qn(B_qn), .reset(Reset_out));  // open: preset
  and and_6 (and_6_out, A_qn, B_qn);
  and and_7 (and_7_out, A_q, B_qn);
  and and_8 (and_8_out, A_qn, B_q);
  and and_9 (and_9_out, B_q, A_q);
  or or_3 (or_3_out, and_7_out, and_9_out);
  or or_4 (or_4_out, and_6_out, and_8_out);
  LED EW_Red (.in(or_4_out));
  LED NS_green (.in(and_6_out));
  LED NS_Yellow (.in(and_8_out));
  LED EW_Green (.in(and_7_out));
  LED NS_Red (.in(or_3_out));
  LED EW_Yellow (.in(and_9_out));

  // Notes on the sheet:
  //   Austine Iheji and McNobert Amoah
  //   Traffic Light
endmodule

module anotherone (
  input  in_1,
  input  in_2,
  input  in_3,
  input  in_4
);

  wire A_q, A_qn, and_1_out, and_2_out, and_3_out, and_4_out, and_5_out, and_6_out, and_7_out, and_8_out,
       and_9_out, and_10_out, and_11_out, and_12_out, and_13_out, and_14_out, and_15_out, and_16_out,
       and_17_out, and_18_out, B_q, B_qn, button_1_out, clock_1_out, comparator_1_eq, comparator_2_eq,
       comparator_3_eq, comparator_4_eq, d_ff_1_q, d_ff_1_qn, d_ff_2_q, d_ff_2_qn, demultiplexer_1_out0,
       demultiplexer_1_out1, or_1_out, or_2_out, or_3_out, or_4_out, or_5_out, or_6_out, or_7_out, or_8_out,
       Reset_out;
  wire [4:0] counter_1_q, counter_2_q;

  Clock clock_1 (.out(clock_1_out));
  Demultiplexer demultiplexer_1 (
    .out0(demultiplexer_1_out0), .out1(demultiplexer_1_out1), .in(clock_1_out), .sel(in_2));
  Button Reset (.out(Reset_out));
  Button button_1 (.out(button_1_out));
  Counter #(.max('h13), .width(5)) counter_1 (
    .load(in_1), .D(5'b00101), .Q(counter_1_q), .clk(demultiplexer_1_out0), .clr(Reset_out));  // open: count, carry, up
  Counter #(.max('h19), .width(5)) counter_2 (
    .load(in_3), .D(5'b00101), .Q(counter_2_q), .clk(demultiplexer_1_out1), .clr(button_1_out));  // open: count, carry, up
  Comparator #(.width(5)) comparator_1 (.a(counter_1_q), .b(5'b00101), .eq(comparator_1_eq));  // open: gt, lt
  Comparator #(.width(5)) comparator_2 (.a(counter_1_q), .b(5'b10011), .eq(comparator_2_eq));  // open: gt, lt
  Comparator #(.width(5)) comparator_3 (.a(counter_2_q), .b(5'b00101), .eq(comparator_3_eq));  // open: gt, lt
  Comparator #(.width(5)) comparator_4 (.a(counter_2_q), .b(5'b10011), .eq(comparator_4_eq));  // open: gt, lt
  and and_1 (and_1_out, A_q, ~comparator_1_eq);  // AND_Gate
  and and_2 (and_2_out, A_q, ~B_q, ~comparator_2_eq);  // AND_Gate
  and and_3 (and_3_out, ~A_q, comparator_1_eq, B_q, ~comparator_2_eq);  // AND_Gate
  and and_4 (and_4_out, ~comparator_1_eq, comparator_2_eq);  // AND_Gate
  and and_5 (and_5_out, B_q, ~comparator_1_eq);  // AND_Gate
  and and_6 (and_6_out, d_ff_1_q, ~comparator_3_eq);  // AND_Gate
  and and_7 (and_7_out, d_ff_1_q, ~d_ff_2_q, ~comparator_4_eq);  // AND_Gate
  and and_8 (and_8_out, ~d_ff_1_q, comparator_3_eq, d_ff_2_q, ~comparator_4_eq);  // AND_Gate
  and and_9 (and_9_out, ~comparator_3_eq, comparator_4_eq);  // AND_Gate
  and and_10 (and_10_out, d_ff_2_q, ~comparator_3_eq);  // AND_Gate
  or or_1 (or_1_out, and_1_out, and_2_out, and_3_out);
  or or_2 (or_2_out, and_4_out, and_5_out);
  D_Flip_Flop A (.D(or_1_out), .clk(demultiplexer_1_out0), .Q(A_q), .Qn(A_qn), .reset(Reset_out));  // open: preset
  D_Flip_Flop B (.D(or_2_out), .clk(demultiplexer_1_out0), .Q(B_q), .Qn(B_qn), .reset(Reset_out));  // open: preset
  or or_3 (or_3_out, and_6_out, and_7_out, and_8_out);
  or or_4 (or_4_out, and_9_out, and_10_out);
  D_Flip_Flop d_ff_1 (
    .D(or_3_out), .clk(demultiplexer_1_out1), .Q(d_ff_1_q), .Qn(d_ff_1_qn), .reset(button_1_out));  // open: preset
  D_Flip_Flop d_ff_2 (
    .D(or_4_out), .clk(demultiplexer_1_out1), .Q(d_ff_2_q), .Qn(d_ff_2_qn), .reset(button_1_out));  // open: preset
  and and_11 (and_11_out, A_qn, B_qn);
  and and_12 (and_12_out, A_q, B_qn);
  and and_13 (and_13_out, A_qn, B_q);
  and and_14 (and_14_out, B_q, A_q);
  and and_15 (and_15_out, d_ff_1_qn, d_ff_2_qn);
  and and_16 (and_16_out, d_ff_1_q, d_ff_2_qn);
  and and_17 (and_17_out, d_ff_1_qn, d_ff_2_q);
  and and_18 (and_18_out, d_ff_2_q, d_ff_1_q);
  or or_5 (or_5_out, and_12_out, and_14_out);
  or or_6 (or_6_out, and_11_out, and_13_out);
  or or_7 (or_7_out, and_16_out, and_18_out);
  LED EW_Red (.in(or_6_out));
  LED NS_green (.in(and_11_out));
  LED NS_Yellow (.in(and_13_out));
  LED EW_Green (.in(and_12_out));
  LED NS_Red (.in(or_5_out));
  LED EW_Yellow (.in(and_14_out));
  or or_8 (or_8_out, and_15_out, and_17_out);
  LED led_1 (.in(or_8_out));
  LED led_2 (.in(and_15_out));
  LED led_3 (.in(and_17_out));
  LED led_4 (.in(and_16_out));
  LED led_5 (.in(or_7_out));
  LED led_6 (.in(and_18_out));

  // Notes on the sheet:
  //   Traffic Light
  //   Austine Iheji and McNobert Amoah
  //   Austine Iheji and McNobert Amoah
  //   Pedestrain traffic light
endmodule
